# Fritzing sketch Schematic_RPi_RFM69 (saved by Fritzing 0.9.3b)

parts:
  Raspberry_Pi_1 = Raspberry Pi 3 [part_number=RPI-3-V1.2]
  ANT1 = Antenna
  RFM1 = RFM69HCW ISM Transciever

nets:
  3V3: Raspberry_Pi_1.3v3, Raspberry_Pi_1.3V3, RFM1.13_3.3V
  N1: Raspberry_Pi_1.GIPO4, RFM1.12_DIO4
  N2: Raspberry_Pi_1.GIPO17, RFM1.14_DIO0
  N3: Raspberry_Pi_1.GIPO27, RFM1.15_DIO1
  N4: Raspberry_Pi_1.GIPO22, RFM1.11_DIO3
  N5: Raspberry_Pi_1.GIPO10, RFM1.3_MOSI
  N6: Raspberry_Pi_1.GIPO9, RFM1.2_MISO
  N7: Raspberry_Pi_1.GIPO11, RFM1.4_SCK
  N8: Raspberry_Pi_1.GIPO8, RFM1.5_NSS_(CS)
  N9: Raspberry_Pi_1.GIPO25, RFM1.16_DIO2
  N10: Raspberry_Pi_1.GND, RFM1.8_GND
  N11: Raspberry_Pi_1.GIPO24, RFM1.6_RESET
  N12: ANT1.antenna_lead, RFM1.9_ANT

custom parts:
  RFM69HCW ISM Transciever: RF Transceiver by Hope RF. Well supported Arduino libraries are available. This ISM band transceiver is available in several frequencies e.g. 433MHz and 915MHz and it is also available in various feature versions.
